# Fritzing sketch spongeRecovered (saved by Fritzing 0.9.3b)
circuit board: 6.67171cm x 2.8351cm
circuit board: 13cm x 2cm
circuit board: 8.71911cm x 5.59533cm
breadboards: 1

parts:
  FeatherM0 = Adafruit Feather M0 WINC1500 [part_number="Adafruit #3010"]
  R1 = Resistor [tolerance=±5% resistance=1.1k package=THT]
  R2 = Resistor [tolerance=±5% resistance=1.1k package=THT]
  power = Toggle Switch [package=THT]
  S1 = Cherry MX Keyswitch
  S2 = Cherry MX Keyswitch
  S3 = Cherry MX Keyswitch
  S4 = Cherry MX Keyswitch
  Part1 = LSM6DS3(6 DOF)
  Part2 = LSM6DS3(6 DOF)
  fsr1 = Basic Force Sensing Resistor (FSR) [package=THT]
  fsr2 = Basic Force Sensing Resistor (FSR) [package=THT]
  J9 = shrouded pin header, 12 pins [form="♂ (shrouded male)"]
  J11 = shrouded pin header, 6 pins [form="♂ (shrouded male)"]
  J10 = shrouded pin header, 12 pins [form="♂ (shrouded male)"]
  J12 = shrouded pin header, 6 pins [form="♂ (shrouded male)"]
  S0 = Cherry MX Keyswitch
  J13 = shrouded pin header, 6 pins [form="♂ (shrouded male)"]
  LED1 = DUO LED RG [package="5 mm [THT]"]
  R3 = Resistor [tolerance=±5% resistance=470 package=THT]

nets:
  N1: FeatherM0.D1, J12.pin3
  N2: FeatherM0.D0, J12.pin2
  N3: FeatherM0.MISO, Part1.MISO/SDO, J9.pin5
  N4: FeatherM0.MOSI, Part1.MOSI/SDA, J9.pin3
  N5: FeatherM0.SCK, Part1.SCL, J9.pin4
  N6: FeatherM0.A5, J9.pin6
  N7: FeatherM0.A4, Part1.CS
  N8: FeatherM0.A3, R3.Pin_1
  N9: FeatherM0.A2, J9.pin8
  N10: FeatherM0.A1, R2.Pin_0, J9.pin12
  N11: FeatherM0.A0, R1.Pin_0, fsr1.pin_0
  GND: FeatherM0.GND, R1.Pin_1, R2.Pin_1, power.COM, Part1.GND, J9.pin1, J12.pin1, LED1.green_anode
  +3V3: FeatherM0.+3V3, Part1.3.3V, fsr1.pin_1, J9.pin2
  N12: FeatherM0.VBAT, LED1.red_anode
  N13: FeatherM0.EN, power.L1
  N14: FeatherM0.D12, J9.pin11
  N15: FeatherM0.D11, J9.pin10
  N16: FeatherM0.D10, J9.pin9
  N17: FeatherM0.D6, J9.pin7
  N18: FeatherM0.D5, J12.pin6
  N19: FeatherM0.SCL, J12.pin5
  N20: FeatherM0.SDA, J12.pin4
  N21: S1.pin_1, S2.pin_1, S3.pin_1, S4.pin_1, S0.pin_1, J13.pin1
  N22: S1.pin_2, J13.pin3
  N23: S2.pin_2, J13.pin4
  N24: S3.pin_2, J13.pin5
  N25: S4.pin_2, J13.pin6
  N26: Part2.GND, J11.pin1, J10.pin1
  N27: Part2.3.3V, fsr2.pin_1, J10.pin2
  N28: Part2.MOSI/SDA, J10.pin3
  N29: Part2.SCL, J10.pin4
  N30: Part2.MISO/SDO, J10.pin5
  N31: Part2.CS, J10.pin6
  N32: fsr2.pin_0, J10.pin12
  N33: J11.pin2, J10.pin7
  N34: J11.pin3, J10.pin8
  N35: J11.pin4, J10.pin9
  N36: J11.pin5, J10.pin10
  N37: J11.pin6, J10.pin11
  N38: S0.pin_2, J13.pin2
  N39: LED1.common_cathode, R3.Pin_0

custom parts:
  Adafruit Feather M0 WINC1500: This is the Adafruit Feather M0 WiFi w/ATWINC1500 - our take on an 'all-in-one' Arduino-compatible + high speed, reliable WiFi with built in USB and battery charging. Its an Adafruit Feather M0 with a WiFi module, ready to rock! Connect your Feather to the Internet with this fine new FCC-certified WiFi module from Atmel. This 802.11bgn-capable WiFi module is the best new thing for networking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
  Cherry MX Keyswitch: Cherry MX Keyswitch button for keyboards
